# Fritzing sketch NeoArt-Circuit Diagram (saved by Fritzing 0.9.3b)
breadboards: 1

parts:
  R1 = BBC MicroBit
  Part1 = 24 NeoPixel Ring [part_number=1586]
  Part2 = 16 NeoPixel Ring [part_number=1463]
  BATT1 = 4xAA Switchable Battery Pack w/Bare Wire
  Part4 = NeoPixel Jewel [part_number=2226]

nets:
  GND: R1.GND, Part1.GND, Part2.GND, BATT1.NEG, Part4.GND
  N1: R1.P0_ANALOG_IN, Part1.IN
  N2: Part1.OUT, Part2.IN
  VDD: Part1.VDD, Part2.VDD, BATT1.POS, Part4.VDD
  N3: Part2.OUT, Part4.IN

custom parts:
  BBC MicroBit: The BBC MICRO:BIT
  24 NeoPixel Ring: 24 ultra bright smart LED NeoPixels are arranged in a circle with 2.6" (66mm) outer diameter. The rings are 'chainable' - connect the output pin of one to the input pin of another. Use only one microcontroller pin to control as many as you can chain together! Each LED is addressable as the driver chip is inside the LED. Each one has ~18mA constant current drive so the color will be very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
  16 NeoPixel Ring: 16 ultra bright smart LED NeoPixels are arranged in a circle with 1.75" (44.5mm) outer diameter. The rings are 'chainable' - connect the output pin of one to the input pin of another. Use only one microcontroller pin to control as many as you can chain together! Each LED is addressable as the driver chip is inside the LED. Each one has ~18mA constant current drive so the color will be very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
  4xAA Switchable Battery Pack w/Bare Wire: 4xAA Switchable Battery Pack with Bare Wire connection
  NeoPixel Jewel: We fit seven of our tiny 5050 (5mm x 5mm) smart RGB LEDs onto a beautiful, round PCB with mounting holes and a chainable design to create what we think is our most elegant (and evening-wear appropriate) NeoPixel board yet. Use only one microcontroller pin to control as many as you can chain together! Each LED is addressable as the driver chip is inside the LED. Each one has ~18mA constant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
